# Fritzing sketch pi webserver (saved by Fritzing 0.9.4)
breadboards: 1

parts:
  Raspberry_Pi_B_rev1 = Raspberry Pi B rev1
  S1 = Momentary Switch [package=ksa_sealed_tac_switch]
  LED1 = smd LED [color="Red (633nm)" package="1206 [SMD]"]
  R1 = Resistor [tolerance=±5% resistance=10k package=THT]
  Part1 = Adafruit PCA9685 PWM/Servo Breakout [part_number=815]
  JACK1 = 2.1mm Barrel Jack with Terminal Block  # not connected
  J1 = Basic Servo
  J2 = Basic Servo

nets:
  3V3: Raspberry_Pi_B_rev1.3V3, S1.4, Part1.VCC
  N1: Raspberry_Pi_B_rev1.GPIO_0, Part1.SDA
  N2: Raspberry_Pi_B_rev1.GPIO_1, Part1.SCL
  GND: Raspberry_Pi_B_rev1.GND, R1.Pin_1, Part1.GND, J1.gnd
  N3: Raspberry_Pi_B_rev1.GPIO_17, S1.1
  N4: Raspberry_Pi_B_rev1.GPIO_4, LED1.anode
  N5: LED1.cathode, R1.Pin_0
  N6: Part1.PWM15, J2.pulse
  VCC: Part1.5.0V, J1.vcc, J2.vcc
  N7: Part1.PWM14, J1.pulse

custom parts:
  Adafruit PCA9685 PWM/Servo Breakout: Using only two pins, control 16 free-running PWM outputs! I2C-controlled PWM driver with a built in clock. Unlike the TLC5940 family, you do not need to continuously send it signal tying up your microcontroller, its completely free running! 5V compliant, which means you can control it from a 3.3V microcontroller and still safely drive up to 6V outputs (this is good for when you want to control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
